// Logisim project adams_extracredit.circ as structural Verilog: 1 circuit, main circuit main
module main (
  input  Wb,
  input  Wa,
  output [1:0] con
);

  wire and_1_out, and_2_out, and_3_out, and_4_out, and_5_out, and_6_out, clock_1_out, or_1_out, or_2_out;

  and and_1 (and_1_out, ~con[0], Wb, ~Wa, ~con[1]);  // AND_Gate
  and and_2 (and_2_out, con[0], ~Wb, ~Wa, ~con[1]);  // AND_Gate
  and and_3 (and_3_out, con[0], Wb, ~Wa, ~con[1]);  // AND_Gate
  and and_4 (and_4_out, ~con[1], ~Wb, Wa, ~con[0]);  // AND_Gate
  and and_5 (and_5_out, con[1], ~Wb, ~Wa, ~con[0]);  // AND_Gate
  and and_6 (and_6_out, con[1], ~Wb, Wa, ~con[0]);  // AND_Gate
  or or_1 (or_1_out, and_1_out, and_2_out, and_3_out);
  or or_2 (or_2_out, and_4_out, and_5_out, and_6_out);
  Clock clock_1 (.out(clock_1_out));
  Register #(.width(1)) c0 (.D(or_1_out), .Q(con[0]), .clk(clock_1_out));  // open: en, clr
  Register #(.width(1)) c1 (.D(or_2_out), .Q(con[1]), .clk(clock_1_out));  // open: en, clr

  // Notes on the sheet:
  //   c1'(c0'WaWb' + c0Wa'Wb' + c0WaWb')
  //   c0'(c1'Wa'Wb + c1Wa'Wb' + c1Wa'Wb)
endmodule
