// Logisim project Calculator.circ as structural Verilog: 6 circuits, main circuit 8-Bit Calculator
module main (
  input  in_1,
  input  in_2,
  input  in_3,
  input  in_4,
  input  in_5,
  input  in_6,
  input  in_7,
  input  in_8
);

  wire button_5_out;
  wire [3:0] button_out, n8_bit_calculator_1_display_3_0, n8_bit_calculator_1_display_7_4;

  Hex_Digit_Display hex_digit_display_1 (.value(n8_bit_calculator_1_display_3_0));  // open: dp
  Hex_Digit_Display hex_digit_display_2 (.value(n8_bit_calculator_1_display_7_4));  // open: dp
  _8_Bit_Calculator u_8_bit_calculator_1 (
    .Display_7_4(n8_bit_calculator_1_display_7_4), .Display_3_0(n8_bit_calculator_1_display_3_0),
    .in_3(in_1), .in_4(in_2), .in_5(in_3), .in_6(in_4), .in_7(in_5), .in_8(in_6), .in_9(in_7), .in_10(in_8),
    .Equals(button_5_out), .Operator(button_out));
  Button button (.out(button_out[0]));
  Button button_2 (.out(button_out[1]));
  Button button_3 (.out(button_out[2]));
  Button button_4 (.out(button_out[3]));
  Button button_5 (.out(button_5_out));
endmodule

module _8_Bit_Calculator (
  input  Equals,
  input  [3:0] Operator,
  input  in_3,
  input  in_4,
  input  in_5,
  input  in_6,
  input  in_7,
  input  in_8,
  input  in_9,
  input  in_10,
  output [3:0] Display_7_4,
  output [3:0] Display_3_0
);

  wire Controller_y, or_1_out;

  Datapath__FP_Part_2 Datapath (
    .Equal(Equals), .Data_Out({Display_7_4, Display_3_0}),
    .Data_In({in_3, in_4, in_5, in_6, in_7, in_8, in_9, in_10}), .Operator_Input(Operator),
    .FSM_Signal(Controller_y));
  Controller__FP_Part_1 Controller (.x0__Operator_press(or_1_out), .x1__Equals_press(Equals), .y(Controller_y));
  or or_1 (or_1_out, Operator[0], Operator[1], Operator[2], Operator[3]);

  // Notes on the sheet:
  //   Operator Select
endmodule

module Controller__FP_Part_1 (
  input  x0__Operator_press,
  input  x1__Equals_press,
  output y
);

  wire and_1_out, and_2_out, and_3_out, and_4_out, clock_1_out, n_out;

  Clock clock_1 (.out(clock_1_out));
  Register #(.width(1)) register_1 (.D(n_out), .Q(y), .clk(clock_1_out));  // open: en, clr
  and and_1 (and_1_out, ~y, ~x0__Operator_press, x1__Equals_press);  // AND_Gate
  and and_2 (and_2_out, y, ~x0__Operator_press, ~x1__Equals_press);  // AND_Gate
  and and_3 (and_3_out, y, ~x0__Operator_press, x1__Equals_press);  // AND_Gate
  and and_4 (and_4_out, y, x0__Operator_press, x1__Equals_press);
  or n (n_out, and_1_out, and_2_out, and_3_out, and_4_out);

  // Notes on the sheet:
  //   n (Next State)
  //   s (Current State)
  //   n = s'x0'x1 + sx0'x1' + sx0'x1 + sx0x1
  //   y = s
endmodule

module Datapath__FP_Part_2 (
  input  [3:0] Operator_Input,
  input  FSM_Signal,
  input  Equal,
  input  [7:0] Data_In,
  output [7:0] Data_Out
);

  wire and_1_out, and_2_out, clock_1_out, not_1_out, not_2_out, or_1_out;
  wire [3:0] register_3_q;
  wire [7:0] alucir_1_result, register_1_q, register_2_q;

  and and_1 (and_1_out, Equal, FSM_Signal);
  and and_2 (and_2_out, or_1_out, not_1_out);
  Register register_1 (.D(Data_In), .en(and_2_out), .Q(register_1_q), .clk(clock_1_out));  // open: clr
  Register register_2 (.D(Data_In), .en(and_1_out), .Q(register_2_q), .clk(not_2_out));  // open: clr
  Multiplexer #(.width(8)) multiplexer_1 (
    .in0(register_1_q), .in1(alucir_1_result), .out(Data_Out), .sel(FSM_Signal), .en(1'b1));
  Register #(.width(4)) register_3 (
    .D(Operator_Input), .en(and_2_out), .Q(register_3_q), .clk(clock_1_out));  // open: clr
  ALUCIR alucir_1 (.Num1(register_1_q), .Num2(register_2_q), .Operator(register_3_q), .Result(alucir_1_result));
  or or_1 (or_1_out, Operator_Input[0], Operator_Input[1], Operator_Input[2], Operator_Input[3]);
  not not_1 (not_1_out, FSM_Signal);
  not not_2 (not_2_out, clock_1_out);
  Clock clock_1 (.out(clock_1_out));
endmodule

module Encoder (
  input  Op0__Divide,
  input  Op1__Multiply,
  input  Op2__Subtract,
  input  Op3__Add,
  output out_5,
  output out_6
);

  or or_1 (out_5, Op2__Subtract, Op3__Add);
  or or_2 (out_6, Op1__Multiply, Op3__Add);
endmodule

// ALU
module ALUCIR (
  input  [7:0] Num1,
  input  [7:0] Num2,
  input  [3:0] Operator,
  output [7:0] Result
);

  wire [1:0] Operator_Decoder_out_6;
  wire [7:0] adder_1_out, divider_1_out, multiplier_1_out, subtractor_1_out;

  Multiplier multiplier_1 (.a(Num1), .b(Num2), .out(multiplier_1_out), .cin({8{1'b0}}));  // open: cout
  Subtractor subtractor_1 (.a(Num1), .b(Num2), .out(subtractor_1_out), .bin(1'b0));  // open: bout
  Divider divider_1 (.a(Num1), .b(Num2), .out(divider_1_out), .upper({8{1'b0}}));  // open: rem
  Adder adder_1 (.a(Num1), .b(Num2), .out(adder_1_out), .cin(1'b0));  // open: cout
  Multiplexer #(.select(2), .width(8), .disabled(0)) multiplexer_1 (
    .in0(divider_1_out), .in1(multiplier_1_out), .in2(subtractor_1_out), .in3(adder_1_out), .out(Result),
    .sel(Operator_Decoder_out_6), .en(1'b1));
  Encoder Operator_Decoder (
    .Op0__Divide(Operator[0]), .Op1__Multiply(Operator[2]), .Op2__Subtract(Operator[1]),
    .Op3__Add(Operator[3]), .out_5(Operator_Decoder_out_6[1]), .out_6(Operator_Decoder_out_6[0]));
endmodule
