// Logisim project Controller.circ as structural Verilog: 1 circuit, main circuit main
module main (
  input  x0__Operator_press,
  input  x1__Equals_press,
  output y
);

  wire and_1_out, and_2_out, and_3_out, and_4_out, clock_1_out, n_out;

  Clock clock_1 (.out(clock_1_out));
  Register #(.width(1)) register_1 (.D(n_out), .Q(y), .clk(clock_1_out));  // open: en, clr
  and and_1 (and_1_out, ~y, ~x0__Operator_press, x1__Equals_press);  // AND_Gate
  and and_2 (and_2_out, y, ~x0__Operator_press, ~x1__Equals_press);  // AND_Gate
  and and_3 (and_3_out, y, ~x0__Operator_press, x1__Equals_press);  // AND_Gate
  and and_4 (and_4_out, y, x0__Operator_press, x1__Equals_press);
  or n (n_out, and_1_out, and_2_out, and_3_out, and_4_out);

  // Notes on the sheet:
  //   n (Next State)
  //   s (Current State)
  //   n = s'x0'x1 + sx0'x1' + sx0'x1 + sx0x1
  //   y = s
endmodule
